# Fritzing sketch LightPursuer_V0.1 (saved by Fritzing 0.9.2b)
breadboards: 1

parts:
  Part2 = Arduino Uno (Rev3)
  R1 = Resistor [tolerance=±5% resistance=220 package=THT]
  R2 = Resistor [tolerance=±5% resistance=220 package=THT]
  R3 = Photocell (LDR) [package=THT]
  R4 = Photocell (LDR) [package=THT]

nets:
  N1: Part2.A3, R2.Pin_0, R4.pin_1
  N2: Part2.A4/SDA, R1.Pin_1, R3.pin_0
  N3: Part2.3V3, R1.Pin_0, R2.Pin_1
  N4: Part2.GND, R3.pin_1, R4.pin_0
